# Fritzing sketch WeatherStation (saved by Fritzing 0.7.1b)
breadboards: 1

parts:
  RTC = Real Time Clock Module - DS1307 RTC Breakout Board
  humidity = Humidity Sensor - HIH-4030 Breakout
  arduino_weather_shield = Arduino Ethernet Shield
  R1 = Resistor [tolerance=±5% resistance=4.7k package=THT]
  C1 = Electrolytic Capacitor [capacitance=1µF package="100 mil [THT, electrolytic]"]
  R2 = Resistor [tolerance=±5% resistance=4.7k package=THT]
  U1 = mystery part, 7 pins [chip_label=MPLA115A1 spacing=300mil]
  Part1 = RJ45
  R3 = Resistor [tolerance=±5% resistance=100k package=THT]
  R4 = Resistor [tolerance=±5% resistance=10k package=THT]
  R5 = Photocell (LDR) [package=THT]
  R6 = Resistor [tolerance=±5% resistance=10k package=THT]

nets:
  5V: RTC.5V, humidity.VCC, arduino_weather_shield.+5V, R1.Pin_0, C1.+, R2.Pin_0, U1.pin7, R5.pin_0, R6.Pin_0
  GND: RTC.GND, humidity.GND, arduino_weather_shield.GND, C1.-, U1.pin6, Part1.pin_2, Part1.pin_4, Part1.pin_5, Part1.pin_7, R3.Pin_0, R4.Pin_1
  N1: RTC.SCL, arduino_weather_shield.A5, R1.Pin_1
  N2: RTC.SDA, arduino_weather_shield.A4, R2.Pin_1
  N3: humidity.OUT, arduino_weather_shield.A0, R3.Pin_1
  N4: arduino_weather_shield.SCK, U1.pin5
  N5: arduino_weather_shield.MISO, U1.pin3
  N6: arduino_weather_shield.MOSI, U1.pin4
  N7: arduino_weather_shield.D6, U1.pin1
  N8: arduino_weather_shield.D5, U1.pin2
  N9: arduino_weather_shield.D3, Part1.pin_8, R6.Pin_1
  N10: arduino_weather_shield.D2, Part1.pin_3
  N11: arduino_weather_shield.A1, R4.Pin_0, R5.pin_1
  N12: arduino_weather_shield.A2, Part1.pin_1

notes:
  SDN - D9
  CSN - D8
  SDO - D12
  SDI - D11
  SCK - D13
  GND - GND
  VDD - VCC
  RJ45 plug
  1 - Wind Vane
  2 - Anemometer
  3 - Anemometer
  4 - Wind Vane
  5 - N.C.
  6 - N.C.
  7 - Rain Gauge
  8 - Rain Gauge
  2,4,6,8 = GND
  RJ45 connector
  -----------
  1 -- |
  -- 2 |
  3 -- |
  -- 4 |
  5 -- | front (plug comes here)
  -- 6 |
  7 -- |
  -- 8 |
  -----------
  * bottom view
